// Logisim project Ex-8-1.circ as structural Verilog: 1 circuit, main circuit main
module main (
  input  in_1,
  input  in_2,
  input  in_3,
  input  [1:0] in_4,
  output out_5
);

  Multiplexer #(.select(2)) multiplexer_1 (
    .in0(in_1), .in1(in_2), .in2(1'b0), .in3(1'b0), .out(out_5), .sel(in_4), .en(in_3));

  // Notes on the sheet:
  //   V.Krishna
  //   RA21104010028
endmodule
