// Logisim project MUX_Implementation.circ as structural Verilog: 1 circuit, main circuit main
module main (
  input  in_1,
  input  in_2,
  input  [2:0] in_3,
  input  in_4,
  output out_5
);

  wire not_1_out, undriven, undriven_3;
  wire [2:0] undriven_2;

  not not_1 (not_1_out, in_1);
  Multiplexer #(.select(3)) multiplexer_1 (
    .in0(undriven), .in1(not_1_out), .in2(undriven), .in3(1'b1), .in4(1'b1), .in5(in_1), .in6(in_1),
    .in7(in_1), .out(out_5), .sel(undriven_2), .en(undriven_3));
endmodule
